# Fritzing sketch wiring (saved by Fritzing 0.9.3b)

parts:
  Bauteil3 = Arduino Pro Mini (5V)
  R1+R2 = Resistor [tolerance=±5% resistance=330 package="2010 [SMD]"]
  S3 = Momentary Switch [package=ksa_sealed_tac_switch]
  U1 = CC1101 [part_number=CC1101]
  LED3 = DUO LED RG [package="5 mm [THT]"]
  R2 = Resistor [tolerance=±5% resistance=330 package="2010 [SMD]"]
  Bauteil4 = RFID-RC522-v2
  LED4 = smd LED [color="Red (633nm)" package="0805 [SMD]"]
  R3 = Resistor [tolerance=±5% resistance=330 package="2010 [SMD]"]
  SG1 = Buzzer 12mm [package=buzzer-ccv-kit]

nets:
  GND: Bauteil3.GND, S3.3, U1.2, LED3.common_cathode, Bauteil4.GND, LED4.cathode, SG1.1
  VCC: Bauteil3.VCC, U1.1, Bauteil4.3.3V
  N1: Bauteil3.A3, SG1.2
  N2: Bauteil3.A0, R3.Pin_0
  N3: Bauteil3.SCK, U1.4, Bauteil4.SCK
  N4: Bauteil3.MISO, U1.5, Bauteil4.MISO
  N5: Bauteil3.MOSI, U1.3, Bauteil4.MOSI
  N6: Bauteil3.D10, U1.8
  N7: Bauteil3.D9, R2.Pin_1
  N8: Bauteil3.D8, S3.1
  N9: Bauteil3.D7, Bauteil4.SDA
  N10: Bauteil3.D6, Bauteil4.RST
  N11: Bauteil3.D4, R1+R2.Pin_1
  N12: Bauteil3.D2, U1.7
  N13: R1+R2.Pin_0, LED3.green_anode
  N14: LED3.red_anode, R2.Pin_0

custom parts:
  RFID-RC522-v2: A simple China made RFID-RC522 Reader; do check the pin labels, as this is a MFRC522 based clone.
